# Fritzing sketch transistor_IR_LED_transmitter (saved by Fritzing 0.9.3b)
breadboards: 1

parts:
  Q1 = TRANSISTOR_NPN [package=to-92]
  V1 = DC Power [voltage=3.3V]
  R1 = Resistor [tolerance=±5% resistance=10k package=THT]
  LED1 = LEDs [package=led10mm]

nets (from the schematic view):
  N1: Q1.E, V1.V-
  N2: Q1.B, R1.Pin_0
  N3: Q1.C, LED1.C
  N4: V1.V+, LED1.A
